// Logisim project RISCV32 (1).circ as structural Verilog: 16 circuits, main circuit main
module main (
);

  wire alusrc_t, and_1_out, bran_t, clk, controlunit_1_branch, controlunit_1_mem2read, controlunit_1_memread,
       controlunit_1_regwrite, jal_t, mw;
  wire [1:0] controlunit_1_aluop;
  wire [2:0] b_func3_t, controlunit_1_instfmt;
  wire [3:0] alucontrol_1_opcode, bit_extender_3_out;
  wire [7:0] bit_extender_1_out, bit_extender_2_out;
  wire [31:0] adder_1_out, adder_2_out, alu_1_datad, imm_t, ins_t, multiplexer_1_out, multiplexer_2_out,
       multiplexer_3_out, pc4_t, pc_t, ram_1_dout, rd, register_1_q, rs1, rs2, shifter_1_out;

  Clock clock_1 (.out(clk));
  ProgramCounter programcounter_1 (.inPC(multiplexer_3_out), .clk(clk), .outPCplus4(pc4_t), .outPC(pc_t));
  Bit_Extender #(.in_width(32), .out_width(8)) bit_extender_1 (.in(pc_t), .out(bit_extender_1_out));
  ROM #(.dataWidth(32)) rom_1 (.addr(bit_extender_1_out), .data(ins_t));
  ControlUnit controlunit_1 (
    .Opcode(ins_t[6:0]), .instfmt(controlunit_1_instfmt), .Branch(controlunit_1_branch),
    .MemRead(controlunit_1_memread), .ALUop(controlunit_1_aluop), .MemWrite(mw), .ALUSrc(alusrc_t),
    .RegWrite(controlunit_1_regwrite), .J(jal_t), .Mem2Read(controlunit_1_mem2read));
  RegisterFile registerfile_1 (
    .rsi1(ins_t[19:15]), .rsi2(ins_t[24:20]), .rdi(ins_t[11:7]), .WriteEnable(controlunit_1_regwrite),
    .clk(clk), .rd(rd), .rs1(rs1), .rs2(rs2));
  Shifter #(.width(32)) shifter_1 (.in(imm_t), .\dist ({5{1'b0}}), .out(shifter_1_out));
  ImmGeneration immgeneration_1 (
    .ins(ins_t), .instFmt(controlunit_1_instfmt), .Jal(jal_t), .imm31_0(imm_t), .b_func3(b_func3_t));
  Adder #(.width(32)) adder_1 (.a(pc_t), .b(shifter_1_out), .out(adder_1_out));  // open: cin, cout
  and and_1 (and_1_out, controlunit_1_branch, bran_t);
  ALUcontrol alucontrol_1 (.Ins(ins_t), .ALUop(controlunit_1_aluop), .Opcode(alucontrol_1_opcode));
  Branch branch_1 (.func3(b_func3_t), .rs1(rs1), .rs2(rs2), .out_4(bran_t));
  Multiplexer #(.width(32)) multiplexer_1 (.in0(rs2), .in1(imm_t), .out(multiplexer_1_out), .sel(alusrc_t));
  Multiplexer #(.width(32)) multiplexer_2 (.in0(pc4_t), .in1(adder_1_out), .out(multiplexer_2_out), .sel(and_1_out));
  ALU alu_1 (.rs1(rs1), .rs2(multiplexer_1_out), .ALUopcode(alucontrol_1_opcode), .dataD(alu_1_datad));
  Bit_Extender #(.in_width(32), .out_width(8)) bit_extender_2 (.in(alu_1_datad), .out(bit_extender_2_out));
  RAM #(.dataWidth(32)) ram_1 (
    .addr(bit_extender_2_out), .we(mw), .oe(controlunit_1_memread), .clk(clk), .din(rs2), .dout(ram_1_dout));
  Adder #(.width(32)) adder_2 (.a(pc_t), .b(imm_t), .out(adder_2_out));  // open: cin, cout
  Multiplexer #(.width(32)) multiplexer_3 (
    .in0(multiplexer_2_out), .in1(adder_2_out), .out(multiplexer_3_out), .sel(jal_t));
  Multiplexer #(.width(32)) multiplexer_4 (.in0(ram_1_dout), .in1(alu_1_datad), .out(rd), .sel(controlunit_1_mem2read));
  Register #(.width(32)) register_1 (.D(rs2), .en(mw), .clk(clk), .Q(register_1_q));  // open: clr
  Bit_Extender #(.in_width(32), .out_width(4)) bit_extender_3 (.in(register_1_q), .out(bit_extender_3_out));
  Hex_Digit_Display hex_digit_display_1 (.value(bit_extender_3_out));  // open: dp
  Hex_Digit_Display hex_digit_display_2 ();  // open: value, dp

  // Other names for the same wires on the sheet: opcode[6:0] = ins_t[6:0]; rdi[4:0] = ins_t[11:7];
  //   rsi1[4:0] = ins_t[19:15]; rsi2[4:0] = ins_t[24:20]

  // Notes on the sheet:
  //   contents of rom_1 (hex, n*v repeats v):
  //   100293 0 0 0 10000317 0 0 0 ffc30313 0 0 0 532023 0 0 0 128293 0 0 0 430313 0 0 0 b00393 0 0 0
  //   fe72c8e3 0 0 0 a00893 0 0 0 73
endmodule

module ProgramCounter (
  input  [31:0] inPC,
  input  clk,
  output [31:0] outPCplus4,
  output [31:0] outPC
);

  Register #(.width(32)) register_1 (.D(inPC), .en(1'b1), .clk(clk), .Q(outPC));  // open: clr
  Adder #(.width(32)) adder_1 (.a(outPC), .b(32'h4), .out(outPCplus4));  // open: cin, cout

  // Other names for the same wires on the sheet: clk_t = clk; inPC_t[31:0] = inPC; outPC_t[31:0] = outPC;
  //   outPCplus4_t[31:0] = outPCplus4
endmodule

module RegisterFile (
  input  [4:0] rsi1,
  input  [4:0] rsi2,
  input  [4:0] rdi,
  input  [31:0] rd,
  input  WriteEnable,
  input  clk,
  output [31:0] rs1,
  output [31:0] rs2
);

  wire x0we_t, x1we_t, x2we_t, x3we_t, x4we_t, x5we_t, x6we_t, x7we_t, x8we_t, x9we_t, x10we_t, x11we_t,
       x12we_t, x13we_t, x14we_t, x15we_t, x16we_t, x17we_t, x18we_t, x19we_t, x20we_t, x21we_t, x22we_t,
       x23we_t, x24we_t, x25we_t, x26we_t, x27we_t, x28we_t, x29we_t, x30we_t, x31we_t;
  wire [31:0] x1q_t, x2q_t, x3q_t, x4q_t, x5q_t, x6q_t, x7q_t, x8q_t, x9q_t, x10q_t, x11q_t, x12q_t, x13q_t,
       x14q_t, x15q_t, x16q_t, x17q_t, x18q_t, x19q_t, x20q_t, x21q_t, x22q_t, x23q_t, x24q_t, x25q_t,
       x26q_t, x27q_t, x28q_t, x29q_t, x30q_t, x31q_t;

  Demultiplexer #(.select(5)) demultiplexer_1 (
    .out0(x0we_t), .out1(x1we_t), .out2(x2we_t), .out3(x3we_t), .out4(x4we_t), .out5(x5we_t), .out6(x6we_t),
    .out7(x7we_t), .out8(x8we_t), .out9(x9we_t), .out10(x10we_t), .out11(x11we_t), .out12(x12we_t),
    .out13(x13we_t), .out14(x14we_t), .out15(x15we_t), .out16(x16we_t), .out17(x17we_t), .out18(x18we_t),
    .out19(x19we_t), .out20(x20we_t), .out21(x21we_t), .out22(x22we_t), .out23(x23we_t), .out24(x24we_t),
    .out25(x25we_t), .out26(x26we_t), .out27(x27we_t), .out28(x28we_t), .out29(x29we_t), .out30(x30we_t),
    .out31(x31we_t), .in(WriteEnable), .sel(rdi));
  Register #(.width(32)) x4 (.D(rd), .en(x4we_t), .clk(clk), .Q(x4q_t));  // open: clr
  Register #(.width(32)) x8 (.D(rd), .en(x8we_t), .clk(clk), .Q(x8q_t));  // open: clr
  Register #(.width(32)) x12 (.D(rd), .en(x12we_t), .clk(clk), .Q(x12q_t));  // open: clr
  Register #(.width(32)) x16 (.D(rd), .en(x16we_t), .clk(clk), .Q(x16q_t));  // open: clr
  Register #(.width(32)) x20 (.D(rd), .en(x20we_t), .clk(clk), .Q(x20q_t));  // open: clr
  Register #(.width(32)) x24 (.D(rd), .en(x24we_t), .clk(clk), .Q(x24q_t));  // open: clr
  Register #(.width(32)) x28 (.D(rd), .en(x28we_t), .clk(clk), .Q(x28q_t));  // open: clr
  Register #(.width(32)) x1 (.D(rd), .en(x1we_t), .clk(clk), .Q(x1q_t));  // open: clr
  Register #(.width(32)) x5 (.D(rd), .en(x5we_t), .clk(clk), .Q(x5q_t));  // open: clr
  Register #(.width(32)) x9 (.D(rd), .en(x9we_t), .clk(clk), .Q(x9q_t));  // open: clr
  Register #(.width(32)) x13 (.D(rd), .en(x13we_t), .clk(clk), .Q(x13q_t));  // open: clr
  Register #(.width(32)) x17 (.D(rd), .en(x17we_t), .clk(clk), .Q(x17q_t));  // open: clr
  Register #(.width(32)) x21 (.D(rd), .en(x21we_t), .clk(clk), .Q(x21q_t));  // open: clr
  Register #(.width(32)) x25 (.D(rd), .en(x25we_t), .clk(clk), .Q(x25q_t));  // open: clr
  Register #(.width(32)) x29 (.D(rd), .en(x29we_t), .clk(clk), .Q(x29q_t));  // open: clr
  Register #(.width(32)) x2 (.D(rd), .en(x2we_t), .clk(clk), .Q(x2q_t));  // open: clr
  Register #(.width(32)) x6 (.D(rd), .en(x6we_t), .clk(clk), .Q(x6q_t));  // open: clr
  Register #(.width(32)) x10 (.D(rd), .en(x10we_t), .clk(clk), .Q(x10q_t));  // open: clr
  Register #(.width(32)) x14 (.D(rd), .en(x14we_t), .clk(clk), .Q(x14q_t));  // open: clr
  Register #(.width(32)) x18 (.D(rd), .en(x18we_t), .clk(clk), .Q(x18q_t));  // open: clr
  Register #(.width(32)) x22 (.D(rd), .en(x22we_t), .clk(clk), .Q(x22q_t));  // open: clr
  Register #(.width(32)) x26 (.D(rd), .en(x26we_t), .clk(clk), .Q(x26q_t));  // open: clr
  Register #(.width(32)) x30 (.D(rd), .en(x30we_t), .clk(clk), .Q(x30q_t));  // open: clr
  Register #(.width(32)) x3 (.D(rd), .en(x3we_t), .clk(clk), .Q(x3q_t));  // open: clr
  Register #(.width(32)) x7 (.D(rd), .en(x7we_t), .clk(clk), .Q(x7q_t));  // open: clr
  Register #(.width(32)) x11 (.D(rd), .en(x11we_t), .clk(clk), .Q(x11q_t));  // open: clr
  Register #(.width(32)) x15 (.D(rd), .en(x15we_t), .clk(clk), .Q(x15q_t));  // open: clr
  Register #(.width(32)) x19 (.D(rd), .en(x19we_t), .clk(clk), .Q(x19q_t));  // open: clr
  Register #(.width(32)) x23 (.D(rd), .en(x23we_t), .clk(clk), .Q(x23q_t));  // open: clr
  Register #(.width(32)) x27 (.D(rd), .en(x27we_t), .clk(clk), .Q(x27q_t));  // open: clr
  Register #(.width(32)) x31 (.D(rd), .en(x31we_t), .clk(clk), .Q(x31q_t));  // open: clr
  Multiplexer #(.select(5), .width(32)) multiplexer_1 (
    .in0({32{1'b0}}), .in1(x1q_t), .in2(x2q_t), .in3(x3q_t), .in4(x4q_t), .in5(x5q_t), .in6(x6q_t),
    .in7(x7q_t), .in8(x8q_t), .in9(x9q_t), .in10(x10q_t), .in11(x11q_t), .in12(x12q_t), .in13(x13q_t),
    .in14(x14q_t), .in15(x15q_t), .in16(x16q_t), .in17(x17q_t), .in18(x18q_t), .in19(x19q_t), .in20(x20q_t),
    .in21(x21q_t), .in22(x22q_t), .in23(x23q_t), .in24(x24q_t), .in25(x25q_t), .in26(x26q_t), .in27(x27q_t),
    .in28(x28q_t), .in29(x29q_t), .in30(x30q_t), .in31(x31q_t), .out(rs1), .sel(rsi1));
  Multiplexer #(.select(5), .width(32)) multiplexer_2 (
    .in0({32{1'b0}}), .in1(x1q_t), .in2(x2q_t), .in3(x3q_t), .in4(x4q_t), .in5(x5q_t), .in6(x6q_t),
    .in7(x7q_t), .in8(x8q_t), .in9(x9q_t), .in10(x10q_t), .in11(x11q_t), .in12(x12q_t), .in13(x13q_t),
    .in14(x14q_t), .in15(x15q_t), .in16(x16q_t), .in17(x17q_t), .in18(x18q_t), .in19(x19q_t), .in20(x20q_t),
    .in21(x21q_t), .in22(x22q_t), .in23(x23q_t), .in24(x24q_t), .in25(x25q_t), .in26(x26q_t), .in27(x27q_t),
    .in28(x28q_t), .in29(x29q_t), .in30(x30q_t), .in31(x31q_t), .out(rs2), .sel(rsi2));

  // Other names for the same wires on the sheet: clk_t = clk; rd_t[31:0] = rd; rdi_t[4:0] = rdi; rs1_t[31:0] = rs1;
  //   rs2_t[31:0] = rs2; rsi1_t[4:0] = rsi1; rsi2_t[4:0] = rsi2; we_t = WriteEnable
endmodule

module ALU (
  input  [31:0] rs1,
  input  [31:0] rs2,
  input  [3:0] ALUopcode,
  output [31:0] dataD
);

  wire comparator_1_lt, comparator_2_lt;
  wire [31:0] addOut, andOut, orOut, sllOut, sltOut, sltuOut, sraOut, srlOut, subOut, xorOut;

  assign orOut = rs1 | rs2;  // OR_Gate or_1, 32 bits wide
  assign andOut = rs1 & rs2;  // AND_Gate and_1, 32 bits wide
  Adder #(.width(32)) adder_1 (.a(rs1), .b(rs2), .out(addOut));  // open: cin, cout
  Subtractor #(.width(32)) subtractor_1 (.a(rs1), .b(rs2), .out(subOut));  // open: bin, bout
  Shifter #(.width(32)) shifter_1 (.in(rs1), .\dist (rs2[4:0]), .out(sllOut));
  Comparator #(.width(32)) comparator_1 (.a(rs1), .b(rs2), .lt(comparator_1_lt));  // open: gt, eq
  assign sltOut = {{31{1'b0}}, comparator_1_lt};  // Bit_Extender bit_extender_1
  Comparator #(.mode("unsigned"), .width(32)) comparator_2 (.a(rs1), .b(rs2), .lt(comparator_2_lt));  // open: gt, eq
  assign sltuOut = {{31{1'b0}}, comparator_2_lt};  // Bit_Extender bit_extender_2
  assign xorOut = rs1 ^ rs2;  // XOR_Gate xor_1, 32 bits wide
  Shifter #(.shift("lr"), .width(32)) shifter_2 (.in(rs1), .\dist (rs2[4:0]), .out(srlOut));
  Shifter #(.shift("ar"), .width(32)) shifter_3 (.in(rs1), .\dist (rs2[4:0]), .out(sraOut));
  Multiplexer #(.select(4), .width(32)) multiplexer_1 (
    .in0(addOut), .in1(sllOut), .in2(sltOut), .in3(sltuOut), .in4(xorOut), .in5(srlOut), .in6(orOut),
    .in7(andOut), .in8(subOut), .in13(sraOut), .out(dataD), .sel(ALUopcode));  // open: in9, in10, in11, in12, in14, in15

  // Other names for the same wires on the sheet: dataA_t[31:0] = rs1; dataB_t[31:0] = rs2; dataBL5_t[4:0] = rs2[4:0];
  //   dataD_t[31:0] = dataD; sel_t[3:0] = ALUopcode

  // Notes on the sheet:
  //   Opcode
  //   0000
  //   1000
  //   0001
  //   0001
  //   0010
  //   0010
  //   0011
  //   0011
  //   0100
  //   0100
  //   0101
  //   0101
  //   1101
  //   1101
  //   0110
  //   0110
  //   0111
  //   0111
  //   RV32I ALU Operations
  //   Operation
  //   add
  //   add
  //   sub
  //   sll
  //   sll
  //   slt
  //   slt
  //   sltu
  //   sltu
  //   xor
  //   xor
  //   srl
  //   srl
  //   sra
  //   sra
  //   or
  //   or
  //   and
  //   and
  //   Opcode
  //   RV32I ALU Operations
  //   0000
  //   1000
  //   Operation
  //   sub
endmodule

module Branch (
  input  [31:0] rs1,
  input  [31:0] rs2,
  input  [2:0] func3,
  output out_4
);

  wire brEn_t, brEq_t, brEqu_t, brGe_t, brGeu_t, brLt_t, brLtu_t, or_1_out, or_2_out;

  Comparator #(.width(32)) comparator_1 (.a(rs1), .b(rs2), .gt(brGe_t), .eq(brEq_t), .lt(brLt_t));
  Comparator #(.mode("unsigned"), .width(32)) comparator_2 (.a(rs1), .b(rs2), .gt(brGeu_t), .eq(brEqu_t), .lt(brLtu_t));
  not not_1 (brEn_t, brEq_t);
  or or_1 (or_1_out, brGe_t, brEq_t);
  or or_2 (or_2_out, brGeu_t, brEqu_t);
  Multiplexer #(.select(3)) multiplexer_1 (
    .in0(brEq_t), .in1(brEn_t), .in4(brLt_t), .in5(or_1_out), .in6(brLtu_t), .in7(or_2_out), .out(out_4),
    .sel(func3));  // open: in2, in3

  // Other names for the same wires on the sheet: branch = out_4; dataA_t[31:0] = rs1; dataB_t[31:0] = rs2;
  //   func3_t[2:0] = func3
endmodule

module ImmGeneration (
  input  [31:0] ins,
  input  [2:0] instFmt,
  input  Jal,
  output [31:0] imm31_0,
  output [2:0] b_func3
);

  wire b_imm11_t, imm12_t, imm20_t, j_imm11_t;
  wire [3:0] imm4_1_t;
  wire [4:0] ssplitter_1_imm4_0;
  wire [5:0] imm10_5_t;
  wire [6:0] ssplitter_1_imm11_5;
  wire [7:0] imm19_12_t;
  wire [9:0] imm10_1_t;
  wire [11:0] isplitter_1_imm11_0;
  wire [31:0] BOut_t, IOut_t, JOut_t, SOut_t;
  wire [31:12] UOut_t;

  ISplitter isplitter_1 (.ins(ins), .imm11_0(isplitter_1_imm11_0));  // open: opcode, rd, func3, rs1
  SSplitter ssplitter_1 (
    .ins(ins), .imm4_0(ssplitter_1_imm4_0), .imm11_5(ssplitter_1_imm11_5));  // open: opcode, func3, rs1, rs2
  BSplitter bsplitter_1 (
    .ins(ins), .imm11(b_imm11_t), .imm4_1(imm4_1_t), .func3(b_func3), .imm10_5(imm10_5_t), .imm12(imm12_t));  // open: opcode, rs1, rs2
  JSplitter jsplitter_1 (
    .ins(ins), .imm19_12(imm19_12_t), .imm11(j_imm11_t), .imm10_1(imm10_1_t), .imm20(imm20_t));  // open: opcode, rd
  USplitter usplitter_1 (.ins(ins), .imm31_12(UOut_t));  // open: opcode, rd
  assign IOut_t = {{20{isplitter_1_imm11_0[11]}}, isplitter_1_imm11_0};  // Bit_Extender bit_extender_1
  assign SOut_t = {{20{ssplitter_1_imm11_5[6]}}, {ssplitter_1_imm11_5, ssplitter_1_imm4_0}};  // Bit_Extender bit_extender_2
  assign BOut_t = {{19{imm12_t}}, {imm12_t, b_imm11_t, imm10_5_t, imm4_1_t, 1'b0}};  // Bit_Extender bit_extender_3
  assign JOut_t = {{11{imm20_t}}, {imm20_t, imm19_12_t, j_imm11_t, imm10_1_t, 1'b0}};  // Bit_Extender bit_extender_4
  Multiplexer #(.select(3), .width(32)) multiplexer_1 (
    .in0(IOut_t), .in1(SOut_t), .in2(BOut_t), .in3(JOut_t), .in4({UOut_t, {12{1'b0}}}), .out(imm31_0),
    .sel(instFmt));  // open: in5, in6, in7

  // Other names for the same wires on the sheet: b_func3_t[2:0] = b_func3; imm31_0_t[31:0] = imm31_0;
  //   ins_t[31:0] = ins; J_t = Jal; sel_t[2:0] = instFmt
endmodule

module ISplitter (
  input  [31:0] ins,
  output [6:0] opcode,
  output [4:0] rd,
  output [2:0] func3,
  output [4:0] rs1,
  output [11:0] imm11_0
);


  assign func3 = ins[14:12];
  assign imm11_0 = ins[31:20];
  assign opcode = ins[6:0];
  assign rd = ins[11:7];
  assign rs1 = ins[19:15];

  // Notes on the sheet:
  //   ISplitter
endmodule

module SSplitter (
  input  [31:0] ins,
  output [6:0] opcode,
  output [4:0] imm4_0,
  output [2:0] func3,
  output [4:0] rs1,
  output [4:0] rs2,
  output [6:0] imm11_5
);


  assign func3 = ins[14:12];
  assign imm4_0 = ins[11:7];
  assign imm11_5 = ins[31:25];
  assign opcode = ins[6:0];
  assign rs1 = ins[19:15];
  assign rs2 = ins[24:20];

  // Notes on the sheet:
  //   SSplitter
endmodule

module USplitter (
  input  [31:0] ins,
  output [6:0] opcode,
  output [4:0] rd,
  output [19:0] imm31_12
);


  assign imm31_12 = ins[31:12];
  assign opcode = ins[6:0];
  assign rd = ins[11:7];

  // Notes on the sheet:
  //   USplitter
endmodule

module JSplitter (
  input  [31:0] ins,
  output [6:0] opcode,
  output [4:0] rd,
  output [7:0] imm19_12,
  output imm11,
  output [9:0] imm10_1,
  output imm20
);


  assign imm10_1 = ins[30:21];
  assign imm11 = ins[20];
  assign imm19_12 = ins[19:12];
  assign imm20 = ins[31];
  assign opcode = ins[6:0];
  assign rd = ins[11:7];

  // Notes on the sheet:
  //   JSplitter
endmodule

module BSplitter (
  input  [31:0] ins,
  output [6:0] opcode,
  output imm11,
  output [3:0] imm4_1,
  output [2:0] func3,
  output [4:0] rs1,
  output [4:0] rs2,
  output [5:0] imm10_5,
  output imm12
);


  assign func3 = ins[14:12];
  assign imm4_1 = ins[11:8];
  assign imm10_5 = ins[30:25];
  assign imm11 = ins[7];
  assign imm12 = ins[31];
  assign opcode = ins[6:0];
  assign rs1 = ins[19:15];
  assign rs2 = ins[24:20];

  // Notes on the sheet:
  //   BSplitter
endmodule

module RSplitter (
  input  [31:0] ins,
  output [6:0] opcode,
  output [4:0] rd,
  output [2:0] func3,
  output [4:0] rs1,
  output [4:0] rs2,
  output [6:0] func7
);


  assign func3 = ins[14:12];
  assign func7 = ins[31:25];
  assign opcode = ins[6:0];
  assign rd = ins[11:7];
  assign rs1 = ins[19:15];
  assign rs2 = ins[24:20];

  // Notes on the sheet:
  //   RSplitter
endmodule

module ALUcontrol (
  input  [31:0] Ins,
  input  [1:0] ALUop,
  output [3:0] Opcode
);

  wire func3_0_t, func3_1_t, func3_2_t, func7_0_t, func7_1_t, func7_2_t, func7_3_t, func7_4_t, func7_5_t,
       func7_6_t;

  RSplitter rsplitter_1 (
    .ins(Ins), .func3({func3_2_t, func3_1_t, func3_0_t}),
    .func7({func7_6_t, func7_5_t, func7_4_t, func7_3_t, func7_2_t, func7_1_t, func7_0_t}));  // open: opcode, rd, rs1, rs2
  PLA #(.in_width(12), .out_width(4), .\table ("00xxxxxxxxxx 0000 # LW\n00xxxxxxxxxx 0000 # SW\nx1xxxxxxxxxx 1000 # BEQ\n1x0000000000 0000 # ADD\n1x0100000000 1000 # SUB\n1x0000000001 0001 # SLL\n1x0000000010 0010 # SLT\n1x0000000011 0011 # SLTU\n1x0000000100 0100 # XOR\n1x0000000101 0101 # SRL\n1x0100000101 1101 # SRA\n1x0000000110 0110 # OR\n1x0000000111 0111 # AND")) pla_1 (
    .in({ALUop, func7_6_t, func7_5_t, func7_4_t, func7_3_t, func7_2_t, func7_1_t, func7_0_t, func3_2_t, func3_1_t, func3_0_t}),
    .out(Opcode));

  // Other names for the same wires on the sheet: func3_t[2:0] = {func3_2_t, func3_1_t, func3_0_t};
  //   func7_t[6:0] = {func7_6_t, func7_5_t, func7_4_t, func7_3_t, func7_2_t, func7_1_t, func7_0_t};
  //   aluop_0_t = ALUop[0]; aluop_1_t = ALUop[1]; opcode_0_t = Opcode[0]; opcode_1_t = Opcode[1];
  //   opcode_2_t = Opcode[2]; opcode_3_t = Opcode[3]

  // Notes on the sheet:
  //   RV32I ALU Operations
  //   Opcode
  //   0000
  //   1000
  //   0001
  //   0010
  //   0011
  //   0100
  //   0101
  //   1101
  //   0110
  //   0111
  //   Operation
  //   add
  //   sub
  //   sll
  //   slt
  //   sltu
  //   xor
  //   srl
  //   sra
  //   or
  //   and
endmodule

module ControlUnit (
  input  [6:0] Opcode,
  output [2:0] instfmt,
  output Branch,
  output MemRead,
  output Mem2Read,
  output [1:0] ALUop,
  output MemWrite,
  output ALUSrc,
  output RegWrite,
  output J
);

  wire auipc_t, Itype_out, jtype_t, Ld_out;

  and RType (ALUop[1], Opcode[0], Opcode[1], ~Opcode[2], ~Opcode[3], Opcode[4], Opcode[5], ~Opcode[6]);  // AND_Gate
  and Ld (Ld_out, Opcode[0], Opcode[1], ~Opcode[2], ~Opcode[3], ~Opcode[4], ~Opcode[5], ~Opcode[6]);  // AND_Gate
  and Sd (MemWrite, Opcode[0], Opcode[1], ~Opcode[2], ~Opcode[3], ~Opcode[4], Opcode[5], ~Opcode[6]);  // AND_Gate
  and beq (ALUop[0], Opcode[0], Opcode[1], ~Opcode[2], ~Opcode[3], ~Opcode[4], Opcode[5], Opcode[6]);  // AND_Gate
  or or_1 (MemRead, Ld_out, auipc_t, Itype_out);
  and Itype (Itype_out, Opcode[0], Opcode[1], ~Opcode[2], ~Opcode[3], Opcode[4], ~Opcode[5], ~Opcode[6]);  // AND_Gate
  and Jtype (jtype_t, Opcode[0], Opcode[1], Opcode[2], ~Opcode[3], Opcode[4], Opcode[5], ~Opcode[6]);  // AND_Gate
  and auipc (auipc_t, Opcode[0], Opcode[1], Opcode[2], ~Opcode[3], Opcode[4], ~Opcode[5], ~Opcode[6]);  // AND_Gate
  and Jal (J, Opcode[0], Opcode[1], Opcode[2], Opcode[3], ~Opcode[4], Opcode[5], Opcode[6]);  // AND_Gate
  PLA #(.in_width(7), .out_width(3), .\table ("0000011 000 # Ld\n1100111 000 # jarl\n0010011 000 # Itype\n0100011 001 # sd\n1100011 010 # brn\n0110111 100 # lui\n0010111 100 # auipc\n1101111 011 # jal")) pla_1 (
    .in(Opcode), .out(instfmt));
  or or_2 (RegWrite, MemRead, ALUop[1], jtype_t, J);
  or or_3 (Mem2Read, ALUop[1], MemRead, jtype_t, J);
  or or_4 (ALUSrc, MemRead, MemWrite, jtype_t, J);

  assign Branch = ALUop[0];

  // Other names for the same wires on the sheet: beq_t = ALUop[0]; rtype_t = ALUop[1]; jal_t = J; ld_t = MemRead;
  //   Sd_t = MemWrite

  // Notes on the sheet:
  //   I
  //   S
  //   B
  //   J
  //   U
  //   000
  //   001
  //   010
  //   011
  //   100
endmodule

module Jal (
  input  [31:0] imm32,
  input  [31:0] PC4,
  output [31:0] imm31_0
);

  wire J_t;

  Multiplexer #(.width(32)) multiplexer_1 (.in0(imm32), .in1(PC4), .out(imm31_0), .sel(J_t));

  // Other names for the same wires on the sheet: imm31_0_t[31:0] = imm32; PC4_t[31:0] = PC4
endmodule

module JUMP (
  input  [31:0] PC,
  input  [31:0] offset,
  output [31:0] out_3,
  output [31:0] NewPC
);

  Multiplier #(.width(32)) multiplier_1 (.a(offset), .b(32'h2), .out(out_3));  // open: cin, cout
  // XOR_Gate xor_1 is placed but not wired
endmodule
